# Fritzing sketch wiring (saved by Fritzing 0.9.3b)
perfboards: 1

parts:
  WeMos_D1_Mini1 = WeMos D1 Mini
  IC1 = ULN2003A [package="DIP16 [THT]"]
  R3 = Resistor [tolerance=±5% resistance=1.2 package=THT]  # not connected
  R4 = Resistor [tolerance=±5% resistance=1M package=THT]
  R5 = Resistor [tolerance=±5% resistance=147k package=THT]  # not connected
  J1 = screw terminal, 3 pins
  J3 = Terminal Block - 3 pins [package=THT]
  J4 = Terminal Block - 2 pins [package=THT]
  R6 = Resistor [tolerance=±5% resistance=10k package=THT]
  J6 = Terminal Block - 2 pins [package=THT]
  R7 = Resistor [tolerance=±5% resistance=330 package=THT]
  R1 = Resistor [tolerance=±5% resistance=1k package=THT]
  R2 = Resistor [tolerance=±5% resistance=1.2 package=THT]
  U1 = TSR12450

nets:
  N1: WeMos_D1_Mini1.3V3, J4.Line_2
  N2: WeMos_D1_Mini1.5V, U1.OUT
  N3: WeMos_D1_Mini1.D5, R4.Pin_1
  N4: WeMos_D1_Mini1.D6, R1.Pin_1
  N5: WeMos_D1_Mini1.D7, J6.Line_2
  N6: WeMos_D1_Mini1.G, IC1.0V
  N7: IC1.In_1, R1.Pin_0
  N8: IC1.Out_1, R2.Pin_0
  N9: J1.pin1, J3.Line_3, R2.Pin_1
  N10: J1.pin3, J3.Line_2, U1.GND
  N11: J3.Line_1, U1.IN
  N12: J4.Line_1, R6.Pin_0
  N13: J6.Line_1, R7.Pin_0

notes:
  A (24V Bus)
  B (GND Bus)
  P (24V)

custom parts:
  Terminal Block - 3 pins: Generic Screw Terminal 9.5mm
  Terminal Block - 2 pins: Generic Screw Terminal 9.5mm
  TSR12450: Mini DC/DC Step-Down (Buck) Converter - 5V @ 1A output - TSR12450
